// Digital circuit FSMwithROM.dig as structural Verilog
// This Finite State Machine for the Baby 8 control unit uses a ROM and some
// helper circuits
module FSMwithROM (
  input  clock,
  input  resetn,
  input  C,
  input  Z,
  input  TZ,
  input  useK,
  input  prevK,
  input  svInd,
  input  jump,
  input  [2:0] jop,
  input  math,
  input  imm,
  input  zs,
  input  zd,
  output wFl,
  output A0,
  output sA0,
  output sA7,
  output wIR,
  output wMem,
  output rMem,
  output [1:0] Cin,
  output [1:0] logSel,
  output [1:0] bSel,
  output [1:0] aSel,
  output [3:0] aAd,
  output [3:0] bAd,
  output [3:0] wAd,
  output wReg
);

  wire [1:0] multiplexer_2_out;
  wire [2:0] decSel;
  wire [3:0] selNext;
  wire [6:0] nextuPC, uPC;

  D_FF_AS #(.Bits(7)) u_uPC (.Set(1'b0), .D(nextuPC), .C(clock), .Clr(~resetn), .Q(uPC));  // open: nQ
  Multiplexer #(.Bits(3)) multiplexer_1 (.sel(jump), .in_0({math, multiplexer_2_out}), .in_1(jop), .out(decSel));
  Multiplexer multiplexer_2 (.sel(math), .in_0(zd), .in_1(zd), .out(multiplexer_2_out[0]));
  ROM #(.AddrBits(7), .Bits(32)) microcode (
    .A(uPC), .sel(1'b1),
    .D({wAd, bAd, aAd, aSel, bSel, logSel, Cin, wReg, rMem, wMem, wIR, sA7, sA0, A0, wFl, selNext}));
  // Pins of 1 and 2 bits meet at {zs, zd}
  // Pins of 1 and 2 bits meet at {imm, zd}
  // Pins of 1 and 2 bits meet at multiplexer_2_out

  // Other names for the same wires on the sheet: decSel[3] = jump

  // Notes on the sheet:
  //   C: operation in progress generated a carry
  //   Z: operation in progress is producing a zero result
  //   TZ: the two timer registers both have a zero value
  //   wFl: save flags for later use
  //   A0: replacement for A0 in indirect zero page addressing
  //   sA0: select replacement A0
  //   sA7: select replacement A7
  //   wIR: save idecoded instruction arriving from memory
  //   wMem: write to memory
  //   rMem: read from memory - data is available in the next cycle
  //   Cin: selects what will be used for carry in for adder
  //   logSel: selects logic operation in ALU
  //   bSel: selects B operand for ALU
  //   aSel: selects A operand for ALU
  //   aAd: address for A read port in registers
  //   bAd: address for B read port in registers
  //   wAd: address for write port in registers
  //   wReg: the register indicated by wAd will be written to
  //   useK: current instruction is a cascade version
  //   prevK: previous instruction left data in K
  //   svInd: current zero page address is indirect
  //   jump: current instruction is a control flow operation
  //   jop: selects 1 of 8 jump operations
  //   math: current instruction is a regular math operation
  //   imm: current instruction is a math operation with an 8 bit immediate value
  //   zs: the source for this instruction is a zero page address
  //   zd: the destination for this instruction is a zero page address
endmodule
