// Digital circuit baby8.dig as structural Verilog
module baby8 (
  input  reset,
  input  clock,
  input  interrupt,
  input  [7:0] in0,
  input  [7:0] in1,
  output [7:0] out
);

  wire C, Cin, IR_q, loadInst, or_2_out, signA, signB, wMem, wReg, Z;
  wire [3:0] aAd, bAd, wAd;
  wire [5:0] registers_db_2;
  wire [6:0] multiplexer_2_out, multiplexer_3_out;
  wire [7:0] and_1_out, main_memory_d, multiplexer_1_out, not_1_out, or_1_out, prevR_q, registers_db,
       xor_1_out;
  wire [15:0] registers_da;

  RegisterFile #(.AddrBits(4), .Bits(8)) registers (
    .Din(out), .we(wReg), .Rw(wAd), .C(clock), .Ra(aAd), .Rb(bAd), .Da(registers_da[15:8]),
    .Db({registers_db[7], registers_db_2, registers_db[0]}));
  Multiplexer #(.Selector_Bits(2), .Bits(8)) multiplexer_1 (
    .in_0({registers_db[7], registers_db_2, registers_db[0]}), .in_1(main_memory_d), .in_2(in0), .in_3(in1),
    .out(multiplexer_1_out));  // open: sel
  assign and_1_out = registers_da[15:8] & multiplexer_1_out;  // And and_1, 8 bits wide
  assign or_1_out = registers_da[15:8] | multiplexer_1_out;  // Or or_1, 8 bits wide
  assign xor_1_out = registers_da[15:8] ^ multiplexer_1_out;  // XOr xor_1, 8 bits wide
  assign not_1_out = ~registers_da[15:8];  // Not not_1, 8 bits wide
  Multiplexer #(.Selector_Bits(2), .Bits(8)) multiplexer_2 (
    .in_0(registers_da[15:8]), .in_1(not_1_out), .in_2({8{1'b0}}), .in_3(8'hfe),
    .out({signA, multiplexer_2_out}));  // open: sel
  Multiplexer #(.Selector_Bits(2), .Bits(8)) multiplexer_3 (
    .in_0(and_1_out), .in_1(or_1_out), .in_2(xor_1_out), .in_3(multiplexer_1_out),
    .out({signB, multiplexer_3_out}));  // open: sel
  Multiplexer multiplexer_4 (.in_0(registers_db[7]), .out(registers_da[7]));  // open: sel, in_1
  Multiplexer multiplexer_5 (.in_0(registers_db[0]), .out(registers_da[0]));  // open: sel, in_1
  Add #(.Bits(8)) add_1 (.a({signA, multiplexer_2_out}), .b({signB, multiplexer_3_out}), .c_i(Cin), .s(out), .c_o(C));
  or or_2 (or_2_out, out[0], out[1], out[2], out[3], out[4], out[5], out[6], out[7]);
  not not_2 (Z, or_2_out);
  Register prevR (.D(out[0]), .C(clock), .en(1'b1), .Q(prevR_q[0]));
  BlockRAMDualPort #(.AddrBits(12), .Bits(8)) main_memory (
    .A({registers_da[11:7], registers_db_2, registers_da[0]}), .Din(prevR_q), .str(wMem), .C(clock),
    .D(main_memory_d));
  Register IR (.D(main_memory_d[0]), .C(clock), .en(loadInst), .Q(IR_q));
  // Pins of 1 and 8 bits meet at out
  // Pins of 1 and 8 bits meet at prevR_q
  // Pins of 1 and 8 bits meet at main_memory_d

  // Other names for the same wires on the sheet: N = out[7]; int = interrupt
endmodule
