// Digital circuit baby8_alu.dig as structural Verilog
// This simple circuit can do all the operations needed to execute Baby8 instructions
module baby8_alu (
  input  [1:0] logSel,
  input  [1:0] aSel,
  input  Cin,
  input  [7:0] A,
  input  [7:0] B,
  output [7:0] R,
  output C,
  output Z,
  output N,
  output V
);

  wire [7:0] and_1_out, multiplexer_1_out, multiplexer_2_out, not_1_out, or_1_out, xor_1_out;

  assign and_1_out = A & B;  // And and_1, 8 bits wide
  assign or_1_out = A | B;  // Or or_1, 8 bits wide
  assign xor_1_out = A ^ B;  // XOr xor_1, 8 bits wide
  assign not_1_out = ~A;  // Not not_1, 8 bits wide
  Multiplexer #(.Selector_Bits(2), .Bits(8)) multiplexer_1 (
    .sel(aSel), .in_0(A), .in_1(not_1_out), .in_2({8{1'b0}}), .in_3(8'hfe), .out(multiplexer_1_out));
  Multiplexer #(.Selector_Bits(2), .Bits(8)) multiplexer_2 (
    .sel(logSel), .in_0(and_1_out), .in_1(or_1_out), .in_2(xor_1_out), .in_3(B), .out(multiplexer_2_out));
  flags flags_1 (.R(R), .A(multiplexer_1_out), .B(multiplexer_2_out), .Z(Z), .N(N), .V(V));
  Add #(.Bits(8)) add_1 (.a(multiplexer_1_out), .b(multiplexer_2_out), .c_i(Cin), .s(R), .c_o(C));

  // Notes on the sheet:
  //   R: result of the addition
  //   logSel: select logical operation between A and B or just use B
  //   aSel: select A, inverted A or a constant to be added
  //   C: carry out
  //   Cin: carry in
  //   A: second operand (order only matters for subtraction)
  //   B: first operand
  //   Z: indicates that the result is zero
  //   N: indicates that the result is negative
  //   V: indicates an overflow, where the sign
  //   of the result is different from the signs
  //   of the operands
endmodule
