// Digital circuit baby8_control.dig as structural Verilog
module baby8_control (
  input  [7:0] dIn,
  input  Z,
  input  C,
  input  N,
  input  V,
  input  clock,
  input  resetn,
  input  \int ,
  output wReg,
  output [3:0] wAd,
  output [3:0] aAd,
  output [3:0] bAd,
  output [1:0] bSel,
  output [1:0] logSel,
  output [1:0] aSel,
  output Cin,
  output A7,
  output A0,
  output a7S,
  output a0S,
  output wMem,
  output out3,
  output out2,
  output out1,
  output out0,
  output rMem
);

  wire and_1_out, and_2_out, and_3_out, and_4_out, and_7_out, decode_1_zd, decode_1_zs, imm, jump, k, math,
       nextFetch, prevK, register_3_q, svInd, svZD, svZInc, svZInd, svZIO, svZReg, svZS, test, tr, TZ, useK,
       wFl, wIR, wTH, wTL, wZL;
  wire [1:0] aSelIn, bSelIn, CinIn, logSelIn, svD, svS;
  wire [2:0] decode_1_aluop, jop, svAluOp;
  wire [3:0] aAdIn, bAdIn, decode_1_cond, \reg , wAdIn;

  and and_1 (and_1_out, dIn[2], dIn[3]);
  and and_2 (and_2_out, nextFetch, ~useK);  // And
  and and_3 (and_3_out, ~dIn[4], ~dIn[5], ~dIn[6]);  // And
  Register register_1 (.D(\int ), .C(clock), .en(and_2_out), .Q(A7));
  Register register_2 (.D(and_4_out), .C(clock), .en(wTL), .Q(TZ));
  Register register_3 (.D(Z), .C(clock), .en(wTH), .Q(register_3_q));
  Register #(.Bits(4)) register_4 (.D(dIn[3:0]), .C(clock), .en(wZL), .Q(\reg ));
  Register register_5 (.D(dIn[7]), .C(clock), .en(wZL), .Q(svZInd));
  Register register_6 (.D(dIn[0]), .C(clock), .en(wZL), .Q(svZInc));
  Register register_7 (.D(and_1_out), .C(clock), .en(wZL), .Q(svZIO));
  Register register_8 (.D(and_3_out), .C(clock), .en(wZL), .Q(svZReg));
  decode decode_1 (
    .dIn(dIn), .test(test), .k(k), .zd(decode_1_zd), .zs(decode_1_zs), .math(math), .imm(imm), .jump(jump),
    .jop(jop), .aluOp(decode_1_aluop), .cond(decode_1_cond));
  test test_1 (.flags({V, N, C, Z}), .curInt(A7), .clock(clock), .saveFlags(wFl), .cond(decode_1_cond), .tr(tr));
  and and_4 (and_4_out, Z, register_3_q);
  Register register_9 (.D(useK), .C(clock), .en(wIR), .Q(prevK));
  Register register_10 (.D(k), .C(clock), .en(wIR), .Q(useK));
  Register register_11 (.D(decode_1_zd), .C(clock), .en(wIR), .Q(svZD));
  Register register_12 (.D(decode_1_zs), .C(clock), .en(wIR), .Q(svZS));
  Register #(.Bits(3)) register_13 (.D(decode_1_aluop), .C(clock), .en(wIR), .Q(svAluOp));
  Register #(.Bits(2)) register_14 (.D(decode_1_cond[1:0]), .C(clock), .en(wIR), .Q(svD));
  Register #(.Bits(2)) register_15 (.D(decode_1_cond[3:2]), .C(clock), .en(wIR), .Q(svS));
  FSMwithROM fsmwithrom_1 (
    .clock(clock), .resetn(resetn), .C(C), .Z(Z), .TZ(TZ), .useK(useK), .prevK(prevK), .svInd(svInd),
    .jump(jump), .jop(jop), .math(math), .imm(imm), .zs(svZS), .zd(svZD), .wFl(wFl), .A0(A0), .sA0(a0S),
    .sA7(a7S), .wIR(wIR), .wMem(wMem), .rMem(rMem), .Cin(CinIn), .logSel(logSelIn), .bSel(bSelIn),
    .aSel(aSelIn), .aAd(aAdIn), .bAd(bAdIn), .wAd(wAdIn), .wReg(wReg));
  fsm2control fsm2control_1 (
    .wAdIn(wAdIn), .aAdIn(aAdIn), .bAdIn(bAdIn), .bSelIn(bSelIn), .logSelIn(logSelIn), .aSelIn(aSelIn),
    .CinIn(CinIn), .\reg (\reg ), .svS(svS), .curInt(A7), .svD(svD), .prevK(prevK), .useK(useK),
    .svZIO(svZIO), .svZReg(svZReg), .svZInd(svZInd), .svAluOp(svAluOp), .wAd(wAd), .aAd(aAd), .bAd(bAd),
    .bSel(bSel), .logSel(logSel), .aSel(aSel), .Cin(Cin), .out3(out3), .out2(out2), .out1(out1), .out0(out0));
  and and_5 (wTL, ~wAd[0], and_7_out);  // And
  and and_6 (wTH, wAd[0], and_7_out);
  and and_7 (and_7_out, ~wAd[1], wAd[2], ~wAd[3], wReg);  // And
  and and_8 (wZL, ~wAd[0], wAd[1], wAd[2], ~wAd[3], wReg);  // And

  // Other names for the same wires on the sheet: curInt = A7; ZInd = dIn[7]; sA0 = a0S; sA7 = a7S

  // Notes on the sheet:
  //   dIn: data from external memory
  //   Z: zero flag from ALU
  //   C: carry flag from ALU
  //   N: negative flag from ALU
  //   V: overflow flag from ALU
  //   clock: system clock
  //   resetn: resets system when low
  //   int: interrupt when high
  //   wReg: writes the selected register
  //   wAd: register to write
  //   aAd: register to read for second operand
  //   bAd: register to read for first operand
  //   bSel: use register, memory or i/o as operand
  //   logSel: logical operation
  //   aSel: normal, inverted or constant
  //   Cin: output carry in for ALU
  //   A7: replacement value for A7
  //   A0: replacement value for A0
  //   a7S: use alternative A7
  //   a0S: use alternative A0
  //   wMem: asks memory to save data
  //   out3: output port 3 should load dOut
  //   out2: output port 2 should load dOut
  //   out1: output port 1 should load dOut
  //   out0: output port 0 should load dOut
  //   rMem: asks memory to output data
endmodule
