// Digital circuit baby8cpu.dig as structural Verilog
// Baby 8 is a simple 8 bit von Neumann processor optimized to use as
// few FPGA resources as possible so it can interface different boards to
// a user project
module baby8cpu (
  input  clock,
  input  resetn,
  input  \int ,
  input  [7:0] in0,
  input  [7:0] in1,
  input  [7:0] dIn,
  output [7:0] dOut,
  output [15:0] address,
  output wMem,
  output out3,
  output out2,
  output out1,
  output out0,
  output rMem
);

  wire baby8_control_1_a0, baby8_control_1_a0s, baby8_control_1_a7, baby8_control_1_a7s, baby8_control_1_cin,
       baby8_control_1_wreg, baby8_datapath_1_c, baby8_datapath_1_n, baby8_datapath_1_v, baby8_datapath_1_z;
  wire [1:0] baby8_control_1_asel, baby8_control_1_bsel, baby8_control_1_logsel;
  wire [3:0] baby8_control_1_aad, baby8_control_1_bad, baby8_control_1_wad;

  baby8_control baby8_control_1 (
    .dIn(dIn), .Z(baby8_datapath_1_z), .C(baby8_datapath_1_c), .N(baby8_datapath_1_n),
    .V(baby8_datapath_1_v), .clock(clock), .resetn(resetn), .\int (\int ), .wReg(baby8_control_1_wreg),
    .wAd(baby8_control_1_wad), .aAd(baby8_control_1_aad), .bAd(baby8_control_1_bad),
    .bSel(baby8_control_1_bsel), .logSel(baby8_control_1_logsel), .aSel(baby8_control_1_asel),
    .Cin(baby8_control_1_cin), .A7(baby8_control_1_a7), .A0(baby8_control_1_a0), .a7S(baby8_control_1_a7s),
    .a0S(baby8_control_1_a0s), .wMem(wMem), .out3(out3), .out2(out2), .out1(out1), .out0(out0), .rMem(rMem));
  baby8_datapath baby8_datapath_1 (
    .clock(clock), .in0(in0), .in1(in1), .wReg(baby8_control_1_wreg), .wAd(baby8_control_1_wad),
    .aAd(baby8_control_1_aad), .bAd(baby8_control_1_bad), .dIn(dIn), .bSel(baby8_control_1_bsel),
    .logSel(baby8_control_1_logsel), .Cin(baby8_control_1_cin), .A7(baby8_control_1_a7),
    .A0(baby8_control_1_a0), .a7S(baby8_control_1_a7s), .a0S(baby8_control_1_a0s),
    .aSelf(baby8_control_1_asel), .dOut(dOut), .address(address), .Z(baby8_datapath_1_z),
    .V(baby8_datapath_1_v), .N(baby8_datapath_1_n), .C(baby8_datapath_1_c));

  // Notes on the sheet:
  //   clock: system clock
  //   resetn: resets system when low
  //   int: interrupts when high
  //   dOut: data to memory
  //   address: selects byte to read or write in external memory
  //   wMem: tells memory to save dOut in address
  //   out3: output port 3 should save dOut
  //   out2: output port 2 should save dOut
  //   out1: output port 1 should save dOut
  //   out0: output port 0 should save dOut
  //   in0: data from input port 0
  //   in1: data from input port 1
  //   dIn: data from memory
  //   rMem: tells memory to output data
endmodule
