// Digital circuit cmux.dig as structural Verilog
// special multiplexor that also handles change in PH,PL with interrupt level
module cmux (
  input  [3:0] in3,
  input  [3:0] in2,
  input  [3:0] in1,
  input  [3:0] in0,
  input  curInt,
  output [3:0] out,
  output sel0
);

  wire and_1_out, or_1_out;
  wire [1:0] or_2_out;
  wire [2:2] xor_1_out;

  and and_1 (and_1_out, in3[1], in3[2], in3[3], curInt);
  xor xor_1 (xor_1_out[2], in3[2], and_1_out);
  or or_1 (or_1_out, in3[2], in3[3]);
  or or_2 (or_2_out[0], in3[0], or_1_out);
  or or_3 (or_2_out[1], in3[1], or_1_out);
  Multiplexer #(.Bits(4), .Selector_Bits(2)) multiplexer_1 (
    .sel(or_2_out), .in_0(in0), .in_1(in1), .in_2(in2), .in_3({in3[3], xor_1_out[2], in3[2], in3[0]}),
    .out(out));
  nor nor_1 (sel0, or_2_out[0], or_2_out[1]);

  // Notes on the sheet:
  //   in3: the selection is extracted from this input
  //   curInt: current Interrupt level
endmodule
