// Digital circuit decode.dig as structural Verilog
// converts and incoming byte into signals that detail the features of the corresponding Baby 8 instruction
module decode (
  input  [7:0] dIn,
  output test,
  output k,
  output zd,
  output zs,
  output math,
  output imm,
  output jump,
  output [2:0] jop,
  output [2:0] aluOp,
  output [3:0] cond
);

  wire and_3_out, and_4_out;

  Multiplexer #(.Bits(3)) multiplexer_1 (.sel(imm), .in_0(dIn[7:5]), .in_1(dIn[4:2]), .out(aluOp));
  and and_1 (zd, dIn[0], dIn[1]);
  and and_2 (zs, dIn[2], dIn[3]);
  and and_3 (and_3_out, dIn[5], dIn[6]);
  and and_4 (and_4_out, and_3_out, dIn[7]);
  and and_5 (test, and_3_out, ~dIn[7]);  // And
  and and_6 (jump, zs, and_4_out);
  and and_7 (imm, ~zs, and_4_out);  // And
  and and_8 (math, ~and_4_out, ~test);  // And
  // Pins of 1 and 8 bits meet at dIn
  // Pins of 1 and 3 bits meet at aluOp

  assign cond = dIn[3:0];
  assign jop = {dIn[4], dIn[1:0]};
  assign k = dIn[4];

  // Notes on the sheet:
  //   dIn: Data read from program memory
  //   test: indicates a test instruction
  //   k: indicates cascade instructions depending on the other bits
  //   zd: zero page destination address
  //   zs: zero page source address
  //   math: regular math and logic instructions
  //   imm: immediate math and logic instructions
  //   jump: control flow instructions
  //   jop: selects among 8 possible control flow instructions
  //   aluOp: selects among 3 math and 3 logic operations
  //   cond: selects between 16 conditions for test instructions
endmodule
