// Digital circuit baby8_alu.dig as structural Verilog
// This simple circuit can do all the operations needed to execute Baby8 instructions
module baby8_alu (
  input  [1:0] logSel,
  input  [1:0] aSel,
  input  Cin,
  input  [7:0] A,
  input  [7:0] B,
  output [7:0] R,
  output Z,
  output C,
  output N,
  output V
);

  wire and_2_out, and_3_out, or_3_out;
  wire [7:0] and_1_out, multiplexer_1_out, multiplexer_2_out, not_1_out, or_1_out, xor_1_out;

  assign and_1_out = A & B;  // And and_1, 8 bits wide
  assign or_1_out = A | B;  // Or or_1, 8 bits wide
  assign xor_1_out = A ^ B;  // XOr xor_1, 8 bits wide
  assign not_1_out = ~A;  // Not not_1, 8 bits wide
  Multiplexer #(.Selector_Bits(2), .Bits(8)) multiplexer_1 (
    .sel(aSel), .in_0(A), .in_1(not_1_out), .in_2({8{1'b0}}), .in_3(8'hfe), .out(multiplexer_1_out));
  Multiplexer #(.Selector_Bits(2), .Bits(8)) multiplexer_2 (
    .sel(logSel), .in_0(and_1_out), .in_1(or_1_out), .in_2(xor_1_out), .in_3(B), .out(multiplexer_2_out));
  and and_2 (and_2_out, ~N, multiplexer_1_out[7], multiplexer_2_out[7]);  // And
  and and_3 (and_3_out, N, ~multiplexer_1_out[7], ~multiplexer_2_out[7]);  // And
  or or_2 (V, and_3_out, and_2_out);
  Add #(.Bits(8)) add_1 (.a(multiplexer_1_out), .b(multiplexer_2_out), .c_i(Cin), .s({N, R[6:0]}), .c_o(C));
  or or_3 (or_3_out, R[0], R[1], R[2], R[3], R[4], R[5], R[6], N);
  not not_2 (Z, or_3_out);

  assign R[7] = N;

  // Notes on the sheet:
  //   R: result of the addition
  //   logSel: select logical operation between A and B or just use B
  //   aSel: select A, inverted A or a constant to be added
  //   Z: addition had zero result
  //   C: carry out
  //   N: addition had negative result
  //   Cin: carry in
  //   V: addition overflowed
endmodule
