// Digital circuit baby8_logic.dig as structural Verilog
// This simple circuit can do all the operations needed to execute Baby8 instructions
module baby8_logic (
  input  [1:0] logSel,
  input  [7:0] A,
  input  [7:0] B,
  output [7:0] R
);

  wire [7:0] and_1_out, or_1_out, xor_1_out;

  assign and_1_out = A & B;  // And and_1, 8 bits wide
  assign or_1_out = A | B;  // Or or_1, 8 bits wide
  assign xor_1_out = A ^ B;  // XOr xor_1, 8 bits wide
  Multiplexer #(.Selector_Bits(2), .Bits(8)) multiplexer_1 (
    .sel(logSel), .in_0(and_1_out), .in_1(or_1_out), .in_2(xor_1_out), .in_3(B), .out(R));

  // Notes on the sheet:
  //   R: result of the addition
  //   logSel: select logical operation between A and B or just use B
endmodule
