// Digital circuit register_test.dig as structural Verilog
module register_test (
  input  clk,
  output [1:0] outB,
  output [1:0] outA,
  output memClk,
  output [1:0] rB,
  output [1:0] rA
);

  wire write_out;
  wire [1:0] and_1_out;
  wire [1:1] toggleAddr_out;
  wire [2:0] counter_1_out;

  Counter #(.Bits(5)) counter_1 (.en(1'b1), .C(clk), .clr(1'b0), .out({rA, counter_1_out}));  // open: ovf
  Button toggleAddr (.out(toggleAddr_out[1]));
  assign and_1_out = counter_1_out[1:0] & {2{toggleAddr_out[1]}};  // And and_1, 2 bits wide
  assign rB = rA ^ and_1_out;  // XOr xor_1, 2 bits wide
  Button write (.out(write_out));
  not not_1 (memClk, counter_1_out[2]);
  RegisterFile #(.Bits(2)) registerfile_1 (
    .Din(rA), .we(write_out), .Rw(rA), .C(memClk), .Ra(rA), .Rb(rB), .Da(outA), .Db(outB));
endmodule
