// Digital circuit flags.dig as structural Verilog
// generates the flags based on the result and the signs of the operands
module flags (
  input  [7:0] R,
  input  [7:0] A,
  input  [7:0] B,
  output Z,
  output N,
  output V
);

  wire and_1_out, and_2_out, or_1_out;

  or or_1 (or_1_out, R[0], R[1], R[2], R[3], R[4], R[5], R[6], R[7]);
  and and_1 (and_1_out, ~R[7], B[7], A[7]);  // And
  not not_1 (Z, or_1_out);
  and and_2 (and_2_out, R[7], ~B[7], ~A[7]);  // And
  or or_2 (V, and_2_out, and_1_out);

  assign N = R[7];

  // Notes on the sheet:
  //   Z: addition had zero result
  //   N: addition had negative result
  //   V: addition overflowed
  //   R: output of the adder
  //   A: operando for the adder
  //   B: other operand for the adder
endmodule

/* Test case z:
R Z

0 1
1 0
2 0
254 0
255 0
*/

/* Test case n:
R N

0 0
1 0
2 0
127 0
128 1
254 1
255 1
*/

/* Test case v:
R A B V

0 0 0 0
0 0 128 0
0 128 0 0
0 128 128 1
128 0 0 1
128 0 128 0
128 128 0 0
129 129 129 0
*/
