// Digital circuit fsm2control.dig as structural Verilog
// converts the encoded outputs from the Finite State Machine into the actual
// values used by the datapath
module fsm2control (
  input  [3:0] wAdIn,
  input  [3:0] aAdIn,
  input  [3:0] bAdIn,
  input  [1:0] bSelIn,
  input  [1:0] logSelIn,
  input  [1:0] aSelIn,
  input  [1:0] CinIn,
  input  [3:0] \reg ,
  input  [1:0] svS,
  input  curInt,
  input  [1:0] svD,
  input  prevK,
  input  useK,
  input  svZIO,
  input  svZReg,
  input  svZInd,
  input  [2:0] svAluOp,
  input  tr,
  output [3:0] wAd,
  output [3:0] aAd,
  output [3:0] bAd,
  output [1:0] bSel,
  output [1:0] logSel,
  output [1:0] aSel,
  output Cin,
  output out3,
  output out2,
  output out1,
  output out0
);

  wire and_1_out, cmux_1_sel0, mCin;
  wire [1:0] mA, memz, mL;
  wire [3:0] kD, kD2;

  Multiplexer #(.Bits(2), .Selector_Bits(2)) multiplexer_1 (
    .sel(bSelIn), .in_0(2'b00), .in_1(2'b01), .in_2(memz), .in_3(2'b00), .out(bSel));
  Multiplexer #(.Selector_Bits(2), .Bits(2)) multiplexer_2 (
    .sel(logSelIn), .in_0(2'b11), .in_1(mL), .in_2(2'b10), .in_3(2'b00), .out(logSel));
  Multiplexer #(.Selector_Bits(2), .Bits(2)) multiplexer_3 (
    .sel(aSelIn), .in_0(2'b10), .in_1(2'b11), .in_2(mA), .in_3(2'b00), .out(aSel));
  Multiplexer #(.Selector_Bits(2)) multiplexer_4 (
    .sel(CinIn), .in_0(1'b0), .in_1(1'b1), .in_2(mCin), .in_3(tr), .out(Cin));
  cmux cmux_1 (.in3(wAdIn), .in2(kD2), .in1({2'b00, svD}), .in0(\reg ), .curInt(curInt), .out(wAd), .sel0(cmux_1_sel0));
  Multiplexer #(.Bits(4)) multiplexer_5 (.sel(useK), .in_0({2'b00, svD}), .in_1(4'b0011), .out(kD2));
  Multiplexer #(.Bits(4)) multiplexer_6 (.sel(prevK), .in_0({2'b00, svD}), .in_1(4'b0011), .out(kD));
  cmux cmux_2 (.in3(aAdIn), .in2(4'b0000), .in1(kD), .in0({2'b00, svS}), .curInt(curInt), .out(aAd));  // open: sel0
  cmux cmux_3 (.in3(bAdIn), .in2(4'b0000), .in1(kD), .in0(\reg ), .curInt(curInt), .out(bAd));  // open: sel0
  and and_1 (and_1_out, cmux_1_sel0, svZIO, svZReg);
  Multiplexer #(.Bits(2), .Selector_Bits(3)) multiplexer_7 (
    .sel({svZInd, svZReg, svZIO}), .in_0(2'b01), .in_1(2'b01), .in_2(2'b00), .in_3({1'b1, \reg [0]}),
    .in_4(2'b01), .in_5(2'b01), .in_6(2'b01), .in_7(2'b01), .out(memz));
  Multiplexer #(.Bits(2)) multiplexer_8 (.sel(svAluOp[2]), .in_0(svAluOp[1:0]), .in_1(2'b00), .out(mA));
  Multiplexer #(.Bits(2)) multiplexer_9 (.sel(svAluOp[2]), .in_0(2'b11), .in_1(svAluOp[1:0]), .out(mL));
  and and_2 (mCin, svAluOp[0], ~svAluOp[2]);  // And
  Demultiplexer #(.Selector_Bits(2)) demultiplexer_1 (
    .sel(\reg [1:0]), .in(and_1_out), .out_0(out0), .out_1(out1), .out_2(out2), .out_3(out3));

  // Other names for the same wires on the sheet: r2[1:0] = \reg [1:0]

  // Notes on the sheet:
  //   wAd: register to write
  //   aAd: register to read for second operand
  //   bAd: register to read for first operand
  //   bSel: use register, memory or i/o as operand
  //   logSel: logical operation
  //   aSel: normal, inverted or constant
  //   Cin: output carry in for ALU
  //   out3: output port 3 should load dOut
  //   out2: output port 2 should load dOut
  //   out1: output port 1 should load dOut
  //   out0: output port 0 should load dOut
  //   wAdIn: raw address for register to write
  //   aAdIn: raw address for first operand
  //   bAdIn: raw address for second operand
  //   bSelIn: raw selection of second operand
  //   logSelIn: raw selection of logic operation
  //   aSelIn: raw selection of first operand
  //   CinIn: raw selection of carry in calculation
  //   reg: low 4 bits of zero page address
  //   svS: saved source field in instruction
  //   svD: saved destination field of instruction
  //   prevK: previous instruction was of the cascade type
  //   useK: current instruction is of the cascade type
  //   svZIO: the last zero page address was to an i/o port
  //   svZReg: the last zero page address was in the register range
  //   svZInd: indicates we are in an indirect zero page address
  //   svAluOp: the saved ALU operation bits from the instruction
  //   (only 6 combinations are valid)
  //   tr: test result using saved flags
  //   B
  //   mem
  //   x
  //   ^
  //   0
  //   -2
  //   A
endmodule
