// Digital circuit test.dig as structural Verilog
// This circuit calculates the 16 possible conditions used by the test instruction
// in the same style as the PDP-11 and the ARM processors
module test (
  input  [3:0] flags,
  input  curInt,
  input  clock,
  input  saveFlags,
  input  [3:0] cond,
  output tr
);

  wire and_1_out, and_2_out, and_3_out, and_4_out, c, multiplexer_2_out, n, v, xnor_1_out, xnor_2_out, z;
  wire [3:0] intf_q, normalf_q;

  and and_1 (and_1_out, ~curInt, saveFlags);  // And
  and and_2 (and_2_out, curInt, saveFlags);
  Register #(.Bits(4)) normalf (.D(flags), .C(clock), .en(and_1_out), .Q(normalf_q));
  Register #(.Bits(4)) intf (.D(flags), .C(clock), .en(and_2_out), .Q(intf_q));
  Multiplexer #(.Bits(4)) multiplexer_1 (.sel(curInt), .in_0(normalf_q), .in_1(intf_q), .out({v, n, c, z}));
  and and_3 (and_3_out, n, ~z);  // And
  and and_4 (and_4_out, ~z, c);  // And
  xnor xnor_1 (xnor_1_out, n, v);
  xnor xnor_2 (xnor_2_out, and_3_out, v);
  Multiplexer #(.Selector_Bits(3)) multiplexer_2 (
    .sel(cond[3:1]), .in_0(z), .in_1(c), .in_2(n), .in_3(v), .in_4(and_4_out), .in_5(xnor_1_out),
    .in_6(xnor_2_out), .in_7(1'b1), .out(multiplexer_2_out));
  xor xor_1 (tr, multiplexer_2_out, cond[0]);

  // Notes on the sheet:
  //   flags: the Z, N, C and V bits generated from the ALU
  //   curInt: currently in Interrupt mode
  //   saveFlags: store the current values of the flags for later test instructions
  //   cond: selects between 16 PDP-11/ARM style conditions
  //   tr: test result indicates if the condition selected is true
  //   >
  //   $>=
  //   $>
endmodule
