// Digital circuit test_term.dig as structural Verilog
module test_term (
  input  clk
);

  wire baby8cpu_1_out0, baby8cpu_1_rmem, baby8cpu_1_wmem, rstn_out;
  wire [7:0] _1KB_d, baby8cpu_1_dout;
  wire [15:0] baby8cpu_1_address;

  Reset rstn (.out(rstn_out));
  baby8cpu baby8cpu_1 (
    .clock(clk), .resetn(rstn_out), .\int (1'b0), .in0({8{1'b0}}), .in1({8{1'b0}}), .dIn(_1KB_d),
    .dOut(baby8cpu_1_dout), .address(baby8cpu_1_address), .wMem(baby8cpu_1_wmem), .out0(baby8cpu_1_out0),
    .rMem(baby8cpu_1_rmem));  // open: out3, out2, out1
  RAMDualPort #(.AddrBits(10), .Bits(8)) _1KB (
    .A(baby8cpu_1_address[9:0]), .Din(baby8cpu_1_dout), .str(baby8cpu_1_wmem), .C(clk), .ld(baby8cpu_1_rmem),
    .D(_1KB_d));
  Terminal terminal_1 (.D(baby8cpu_1_dout), .C(clk), .en(baby8cpu_1_out0));
endmodule
